# Fritzing sketch proximity (saved by Fritzing 0.9.3b)
breadboards: 1

parts:
  Part1 = Adafruit Feather M0 WINC1500 [part_number="Adafruit #3010"]
  R2 = Resistor [tolerance=±5% resistance=220 package=THT]
  hc-sr1 = hc-sr04

nets:
  GND: Part1.GND, hc-sr1.GND
  N1: Part1.VBUS, hc-sr1.VCC
  N2: Part1.D12, hc-sr1.Trig
  N3: Part1.D11, R2.Pin_0
  N4: R2.Pin_1, hc-sr1.Echo

notes:
  10K Resistor

custom parts:
  Adafruit Feather M0 WINC1500: This is the Adafruit Feather M0 WiFi w/ATWINC1500 - our take on an 'all-in-one' Arduino-compatible + high speed, reliable WiFi with built in USB and battery charging. Its an Adafruit Feather M0 with a WiFi module, ready to rock! Connect your Feather to the Internet with this fine new FCC-certified WiFi module from Atmel. This 802.11bgn-capable WiFi module is the best new thing for networking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
