# Fritzing sketch slider (saved by Fritzing 0.9.3b)
breadboards: 1

parts:
  Part1 = Adafruit Feather M0 WINC1500 [part_number="Adafruit #3010"]
  R1 = Slide Potentiometer [maximum_resistance=100kΩ]

nets:
  N1: Part1.A1, R1.wiper
  N2: Part1.GND, R1.leg2
  N3: Part1.+3V3, R1.leg1

notes:
  Connect Pin 2 to the Analog Input Pin

custom parts:
  Adafruit Feather M0 WINC1500: This is the Adafruit Feather M0 WiFi w/ATWINC1500 - our take on an 'all-in-one' Arduino-compatible + high speed, reliable WiFi with built in USB and battery charging. Its an Adafruit Feather M0 with a WiFi module, ready to rock! Connect your Feather to the Internet with this fine new FCC-certified WiFi module from Atmel. This 802.11bgn-capable WiFi module is the best new thing for networking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
