# Fritzing sketch singleVibration (saved by Fritzing 0.9.3b)
breadboards: 1

parts:
  Part1 = Adafruit Feather M0 WINC1500 [part_number="Adafruit #3010"]
  Q1 = TIP120 Hi-Current Darlington Transistor
  R1 = Resistor [tolerance=±5% resistance=1k package=THT]
  D2 = P1000K [part_number=P1000K]
  MOTOR1 = Vibration Motor

nets:
  N1: Part1.VBUS, D2.cathode, MOTOR1.NEG
  N2: Part1.D11, R1.Pin_0
  N3: Q1.BASE, R1.Pin_1
  N4: Q1.COLLECTOR, D2.anode, MOTOR1.POS

notes:
  1K Resistor
  This power setup works when you are using a single Vib motor

custom parts:
  Adafruit Feather M0 WINC1500: This is the Adafruit Feather M0 WiFi w/ATWINC1500 - our take on an 'all-in-one' Arduino-compatible + high speed, reliable WiFi with built in USB and battery charging. Its an Adafruit Feather M0 with a WiFi module, ready to rock! Connect your Feather to the Internet with this fine new FCC-certified WiFi module from Atmel. This 802.11bgn-capable WiFi module is the best new thing for networking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
  Vibration Motor: An eccentric vibration motor!
